# Fritzing sketch veroboard_layout (saved by Fritzing 0.9.3b)
perfboards: 1

parts:
  Part1 = Arduino Pro Mini v13
  OLED_I2C1 = OLED 128x64 I2C Monochrome Display
  S1 = Pushbutton [package="[THT]"]
  S2 = Pushbutton [package="[THT]"]
  J1 = Screw terminal - 2 pins [package=THT]
  R1 = Resistor [tolerance=±5% resistance=2.2k package=THT]
  R2 = Resistor [tolerance=±5% resistance=2.2k package=THT]
  J2 = Screw terminal - 2 pins [package=THT]
  J3 = Screw terminal - 2 pins [package=THT]  # not connected
  Q1 = Basic FET N-Channel [package="TO220 [THT]"]
  Q2 = Basic FET N-Channel [package="TO220 [THT]"]
  R3 = Resistor [tolerance=±5% resistance=220 package=THT]  # not connected
  J4 = Screw terminal - 2 pins [package=THT]
  Q3 = PNP-Transistor [package="TO92 [THT]"]  # not connected
  R4 = Resistor [tolerance=±5% resistance=2.2k package=THT]  # not connected
  LED1 = LED - 3mm [color="Green (555nm)" package="3 mm [THT]"]  # not connected
  LED2 = LED - 3mm [color="Green (555nm)" package="3 mm [THT]"]  # not connected

nets:
  N1: Part1.A4, OLED_I2C1.SDA
  N2: Part1.A5, OLED_I2C1.SCK
  N3: Part1.RAW, OLED_I2C1.VDD
  N4: Part1.GND, S1.Pin_3, S1.Pin_4, S2.Pin_1, S2.Pin_2, J1.pin2, R1.Pin_0
  N5: Part1.A2, R1.Pin_1, R2.Pin_0
  N6: Part1.A0, R2.Pin_1
  N7: Part1.D9_PWM, S1.Pin_1, S1.Pin_2
  N8: Part1.D8, OLED_I2C1.GND
  N9: Part1.D7, S2.Pin_3, S2.Pin_4
  N10: J2.pin2, Q1.source, Q2.drain
  N11: Q2.source, J4.pin2
